# Fritzing sketch circuit (saved by Fritzing 0.9.3b)
breadboards: 1

parts:
  Part1 = Arduino Uno (Rev3) - ICSP  # not connected
  1Sheeld1 = 1Sheeld
  LED1 = smd LED [color="Blue (430nm)" package="0805 [SMD]"]
  LED2 = smd LED [color="Yellow (585nm)" package="0805 [SMD]"]
  LED4 = smd LED [color="Red (633nm)" package="0805 [SMD]"]
  LED3 = smd LED [color="Green (555nm)" package="0805 [SMD]"]
  LED5 = smd LED [color="White (6500K)" package="0805 [SMD]"]
  R1 = Resistor [tolerance=±5% resistance=220 package="2010 [SMD]"]
  R2 = Resistor [tolerance=±5% resistance=220 package="2010 [SMD]"]
  R3 = Resistor [tolerance=±5% resistance=220 package="2010 [SMD]"]
  R4 = Resistor [tolerance=±5% resistance=220 package="2010 [SMD]"]
  R5 = Resistor [tolerance=±5% resistance=220 package="2010 [SMD]"]
  LED6 = smd LED [color="Blue (430nm)" package="0805 [SMD]"]
  R6 = Resistor [tolerance=±5% resistance=220 package="2010 [SMD]"]
  R7 = Resistor [tolerance=±5% resistance=220 package="2010 [SMD]"]
  S1 = Pushbutton [package="[THT]"]

nets:
  N1: 1Sheeld1.D6, R7.Pin_1, S1.Pin_3, S1.Pin_4
  N2: 1Sheeld1.D7, R6.Pin_1
  N3: 1Sheeld1.D9, R5.Pin_0
  N4: 1Sheeld1.D10, R4.Pin_0
  N5: 1Sheeld1.D11, R3.Pin_0
  N6: 1Sheeld1.D12, R2.Pin_0
  N7: 1Sheeld1.GND, LED2.cathode, LED4.cathode, LED5.cathode
  N8: 1Sheeld1.5V, S1.Pin_1, S1.Pin_2
  N9: LED1.cathode, LED3.cathode
  N10: LED1.anode, R4.Pin_1
  N11: LED2.anode, R3.Pin_1
  N12: LED4.anode, R2.Pin_1
  N13: LED3.anode, R5.Pin_1
  N14: LED5.anode, R1.Pin_1
  N15: LED6.cathode, R6.Pin_0
  N16: LED6.anode, R7.Pin_0

custom parts:
  1Sheeld: 1Sheeld is a new easily configured shield for Arduino. It is connected to a mobile app that allow the usage of all of Android smartphones' capabilities such as LCD Screen, Gyroscope, Switches, LEDs, Accelerometer, Magnetometer, GSM, Wi-Fi, GPS ...etc. into your Arduino sketch.
